// Logisim project processeur_ARO2.circ as structural Verilog: 23 circuits, main circuit main
module main (
);

  wire clk, high_write_en_s, low_write_en_s, processeur_aro2_1_memory_high_byte_o,
       processeur_aro2_1_memory_ldr_data, processeur_aro2_1_memory_low_byte_o,
       processeur_aro2_1_memory_str_data_o, RESET_out, sysclk;
  wire [0:0] processeur_aro2_1_instr_addr_o;
  wire [7:0] rd_data_high_s, rd_data_low_s, wr_data_high_s, wr_data_low_s;
  wire [14:0] memory_addr_s, processeur_aro2_1_instr_addr_o_2;
  wire [15:0] InstrMemory_data, processeur_aro2_1_memory_wr_data_o, rd_data_s;

  Button RESET (.out(RESET_out));
  Clock #(.highDuration(4), .lowDuration(4)) u_clk (.out(clk));
  Clock u_sysclk (.out(sysclk));
  // Probe on processeur_aro2_1_instr_addr_o_2
  ROM #(.addrWidth(15), .dataWidth(16)) InstrMemory (.addr(processeur_aro2_1_instr_addr_o_2), .data(InstrMemory_data));
  // Probe on InstrMemory_data
  processeur_ARO2 processeur_aro2_1 (
    .instr_data_i(InstrMemory_data), .memory_rd_data_i(rd_data_s), .rst_i(RESET_out), .clk_i(clk),
    .instr_addr_o({processeur_aro2_1_instr_addr_o_2, processeur_aro2_1_instr_addr_o[0]}),
    .memory_addr_o(memory_addr_s), .memory_wr_data_o(processeur_aro2_1_memory_wr_data_o),
    .memory_str_data_o(processeur_aro2_1_memory_str_data_o),
    .memory_ldr_data(processeur_aro2_1_memory_ldr_data),
    .memory_high_byte_o(processeur_aro2_1_memory_high_byte_o),
    .memory_low_byte_o(processeur_aro2_1_memory_low_byte_o));
  // Probe on processeur_aro2_1_instr_addr_o_2
  RAM #(.addrWidth(15), .databus("bibus")) DataMemoryHigh (
    .addr(memory_addr_s), .we(high_write_en_s), .oe(1'b1), .clk(sysclk), .din(wr_data_high_s),
    .dout(rd_data_high_s));
  RAM #(.addrWidth(15), .databus("bibus")) DataMemoryLow (
    .addr(memory_addr_s), .we(low_write_en_s), .oe(1'b1), .clk(sysclk), .din(wr_data_low_s),
    .dout(rd_data_low_s));
  memory_controller memory_controller_1 (
    .wr_data_i(processeur_aro2_1_memory_wr_data_o), .str_data_i(processeur_aro2_1_memory_str_data_o),
    .ldr_data_i(processeur_aro2_1_memory_ldr_data), .high_byte_i(processeur_aro2_1_memory_high_byte_o),
    .low_byte_i(processeur_aro2_1_memory_low_byte_o), .rd_data_high_i(rd_data_high_s),
    .rd_data_low_i(rd_data_low_s), .rd_data_o(rd_data_s), .high_data_o(wr_data_high_s),
    .low_data_o(wr_data_low_s), .high_write_en_o(high_write_en_s), .low_write_en_o(low_write_en_s));

  // Notes on the sheet:
  //   Attention, votre version de Logisim
  //   ne contient pas de tracker. Si vous
  //   enregistrez votre projet, toutes les
  //   informations du tracker seront
  //   définitivement effacées.
  //   contents of InstrMemory (hex, n*v repeats v):
  //   200f 211a 2305 3011 18c2 3201 1a8b 1e8c 391d 2104 8103 4301 8902 708a 7888 5444 5c42 5243 5a44 4010
  //   80 8c0 4310 4244 405c 2002 41c2 43da 4102 109a 2000 2100 1842 d000 200c e00b 2100 11*0 202a 213c
  //   46c0 46c0
endmodule

module memory_controller (
  input  [15:0] wr_data_i,
  input  str_data_i,
  input  ldr_data_i,
  input  high_byte_i,
  input  low_byte_i,
  input  [7:0] rd_data_high_i,
  input  [7:0] rd_data_low_i,
  output [15:0] rd_data_o,
  output [7:0] high_data_o,
  output [7:0] low_data_o,
  output high_write_en_o,
  output low_write_en_o
);

  wire and_3_out, and_4_out, and_5_out, not_1_out;
  wire [7:0] multiplexer_2_out, multiplexer_3_out;

  and and_1 (low_write_en_o, low_byte_i, str_data_i);
  and and_2 (high_write_en_o, high_byte_i, str_data_i);
  and and_3 (and_3_out, low_byte_i, high_byte_i);
  and and_4 (and_4_out, high_byte_i, ~low_byte_i);  // AND_Gate
  not not_1 (not_1_out, and_5_out);
  and and_5 (and_5_out, high_byte_i, low_byte_i);
  Multiplexer #(.width(8), .enable("false")) multiplexer_1 (
    .in0(wr_data_i[7:0]), .in1(wr_data_i[15:8]), .out(high_data_o), .sel(and_3_out));
  Multiplexer #(.width(8), .enable("false")) multiplexer_2 (
    .in0(rd_data_low_i), .in1(rd_data_high_i), .out(multiplexer_2_out), .sel(and_4_out));
  Multiplexer #(.width(8), .enable("false")) multiplexer_3 (
    .in0(rd_data_high_i), .in1({8{1'b0}}), .out(multiplexer_3_out), .sel(not_1_out));
  assign rd_data_o = ldr_data_i ? {multiplexer_3_out, multiplexer_2_out} : 16'bz;  // Controlled_Buffer controlled_buffer_1

  assign low_data_o = wr_data_i[7:0];

  // Other names for the same wires on the sheet: wr_data_high_o[7:0] = high_data_o;
  //   wr_data_low_o[7:0] = wr_data_i[7:0]

  // Notes on the sheet:
  //   Attention, votre version de Logisim
  //   ne contient pas de tracker. Si vous
  //   enregistrez votre projet, toutes les
  //   informations du tracker seront
  //   définitivement effacées.
  //   Write interface
  //   Read interface
endmodule

module processeur_ARO2 (
  input  [15:0] instr_data_i,
  input  [15:0] memory_rd_data_i,
  input  rst_i,
  input  clk_i,
  output [15:0] instr_addr_o,
  output [14:0] memory_addr_o,
  output [15:0] memory_wr_data_o,
  output memory_str_data_o,
  output memory_ldr_data,
  output memory_high_byte_o,
  output memory_low_byte_o
);

  wire decode_1_decode_en_o, execute_en_s, fetch_1_branch_o, fetch_en_s, link_en_s, memory_access_en_s,
       reg_bank_en_s;
  wire [1:0] reg_bank_control_bus_s;
  wire [2:0] adr_reg_d_s, adr_reg_mem_s, adr_reg_n_s, adr_reg_s_s, decode_1_imm3_o;
  wire [3:0] cpsr_s;
  wire [4:0] decode_1_imm5_o, mem_control_bus_s;
  wire [6:0] fetch_control_bus_s;
  wire [7:0] decode_1_imm8_o, decode_1_offset8_o;
  wire [10:0] decode_1_offset11_o;
  wire [14:0] execute_control_bus_s;
  wire [15:0] execute_1_data_out_o, fetch_1_instr_data_o, fetch_1_lr_addr_o, fetch_1_pc_fut_o, jump_adr_s,
       memory_access_1_mem_adr_byte_o, PC_pres_s, reg_mem_read_data_s, reg_n_read_data_s, reg_s_read_data_s;

  // Probe on instr_data_i
  fetch fetch_1 (
    .fetch_en_i(fetch_en_s), .instr_data_i(instr_data_i), .PC_pres_i(PC_pres_s), .branch_addr_i(jump_adr_s),
    .fetch_control_bus_i(fetch_control_bus_s), .cpsr_i(cpsr_s), .clk_i(clk_i), .rst_i(rst_i),
    .instr_addr_o(instr_addr_o), .instr_data_o(fetch_1_instr_data_o), .PC_fut_o(fetch_1_pc_fut_o),
    .LR_addr_o(fetch_1_lr_addr_o), .branch_o(fetch_1_branch_o));
  // Probe on instr_addr_o
  // Probe on jump_adr_s
  decode decode_1 (
    .instr_data_i(fetch_1_instr_data_o), .rst_i(rst_i), .clk_i(clk_i), .adr_reg_d_o(adr_reg_d_s),
    .adr_reg_s_o(adr_reg_s_s), .adr_reg_n_o(adr_reg_n_s), .adr_reg_mem_o(adr_reg_mem_s),
    .imm3_o(decode_1_imm3_o), .imm5_o(decode_1_imm5_o), .offset11_o(decode_1_offset11_o),
    .offset8_o(decode_1_offset8_o), .imm8_o(decode_1_imm8_o),
    .reg_bank_control_bus_o(reg_bank_control_bus_s), .execute_control_bus_o(execute_control_bus_s),
    .mem_control_bus_o(mem_control_bus_s), .fetch_control_bus_o(fetch_control_bus_s), .link_en_o(link_en_s),
    .fetch_en_o(fetch_en_s), .decode_en_o(decode_1_decode_en_o), .reg_bank_en_o(reg_bank_en_s),
    .execute_en_o(execute_en_s), .memory_access_en_o(memory_access_en_s));
  // Probe on decode_1_decode_en_o
  bank_registers bank_registers_1 (
    .clk_i(clk_i), .rst_i(rst_i), .register_d_sel_i(adr_reg_d_s), .register_d_data_i(jump_adr_s),
    .register_s_sel_i(adr_reg_s_s), .register_n_sel_i(adr_reg_n_s), .register_mem_sel_i(adr_reg_mem_s),
    .reg_bank_control_bus_i(reg_bank_control_bus_s), .PC_fut_i(fetch_1_pc_fut_o),
    .LR_addr_i(fetch_1_lr_addr_o), .branch_i(fetch_1_branch_o), .link_en_i(link_en_s),
    .reg_bank_en_i(reg_bank_en_s), .register_s_read_data_o(reg_s_read_data_s),
    .register_n_read_data_o(reg_n_read_data_s), .register_mem_read_data_o(reg_mem_read_data_s),
    .PC_pres_o(PC_pres_s));
  execute execute_1 (
    .reg_data_s_i(reg_s_read_data_s), .reg_data_n_i(reg_n_read_data_s), .imm3(decode_1_imm3_o),
    .imm5(decode_1_imm5_o), .offset_incond(decode_1_offset11_o), .offset_cond(decode_1_offset8_o),
    .imm8(decode_1_imm8_o), .execute_control_bus(execute_control_bus_s), .rst_i(rst_i), .clk_i(clk_i),
    .execute_en_i(execute_en_s), .data_out_o(execute_1_data_out_o), .cpsr_o(cpsr_s));
  memory_access memory_access_1 (
    .mem_data_i(memory_rd_data_i), .reg_data_i(reg_mem_read_data_s), .data_i(execute_1_data_out_o),
    .memory_control_bus_i(mem_control_bus_s), .rst_i(rst_i), .clk_i(clk_i),
    .memory_access_en_i(memory_access_en_s), .mem_data_adr_o(memory_addr_o),
    .mem_adr_byte_o(memory_access_1_mem_adr_byte_o), .mem_data_out_o(memory_wr_data_o),
    .mem_out_o(jump_adr_s), .str_data_o(memory_str_data_o), .ldr_data_o(memory_ldr_data),
    .high_byte_o(memory_high_byte_o), .low_byte_o(memory_low_byte_o));
  // Probe on memory_access_1_mem_adr_byte_o

  // Other names for the same wires on the sheet: clk_s = clk_i; instr_addr_s[15:0] = instr_addr_o;
  //   instr_data_s[15:0] = instr_data_i; memory_addr_s[14:0] = memory_addr_o; memory_high_byte_s = memory_high_byte_o;
  //   memory_ldr_data_s = memory_ldr_data; memory_low_byte_s = memory_low_byte_o;
  //   memory_rd_data_s[15:0] = memory_rd_data_i; memory_str_data_s = memory_str_data_o;
  //   memory_wr_data_s[15:0] = memory_wr_data_o; rst_s = rst_i

  // Notes on the sheet:
  //   Attention, votre version de Logisim
  //   ne contient pas de tracker. Si vous
  //   enregistrez votre projet, toutes les
  //   informations du tracker seront
  //   définitivement effacées.
  //   Intruction memory inputs
  //   Memory interface inputs
  //   Standard inputs
  //   Processeur simplifié pour le cours ARO2
  //   Instruction memory outputs
  //   Memory interface outputs
endmodule

module fetch (
  input  fetch_en_i,
  input  [15:0] instr_data_i,
  input  [15:0] PC_pres_i,
  input  [15:0] branch_addr_i,
  input  [6:0] fetch_control_bus_i,
  input  [3:0] cpsr_i,
  input  clk_i,
  input  rst_i,
  output [15:0] instr_addr_o,
  output [15:0] instr_data_o,
  output [15:0] PC_fut_o,
  output [15:0] LR_addr_o,
  output branch_o
);

  wire cond_test_s;
  wire [15:0] multiplexer_1_out;

  Multiplexer #(.width(16), .enable("false")) multiplexer_1 (
    .in0(LR_addr_o), .in1(branch_addr_i), .out(multiplexer_1_out), .sel(branch_o));
  Adder #(.width(16)) adder_1 (.a(PC_pres_i), .b(16'h2), .out(LR_addr_o), .cin(1'b0));  // open: cout
  and and_1 (branch_o, fetch_control_bus_i[0], cond_test_s);
  Multiplexer #(.width(16), .enable("false")) multiplexer_2 (
    .in0(PC_pres_i), .in1(multiplexer_1_out), .out(PC_fut_o), .sel(fetch_en_i));
  condition_tester condition_tester_1 (
    .cond_en_i(fetch_control_bus_i[1]), .cond_i(fetch_control_bus_i[5:2]), .Z_i(cpsr_i[0]), .C_i(cpsr_i[1]),
    .N_i(cpsr_i[2]), .V_i(cpsr_i[3]), .cond_test_o(cond_test_s));

  assign instr_addr_o = PC_pres_i;
  assign instr_data_o = instr_data_i;

  // Other names for the same wires on the sheet: branch_addr_s[15:0] = branch_addr_i; branch_s = branch_o;
  //   cpsr_s[3:0] = cpsr_i; fetch_control_bus_s[6:0] = fetch_control_bus_i; sel_PC_s = fetch_control_bus_i[0];
  //   cond_en_s = fetch_control_bus_i[1]; cond_s[3:0] = fetch_control_bus_i[5:2]; fetch_en_s = fetch_en_i;
  //   instr_addr_s[15:0] = PC_pres_i; PC_pres_s[15:0] = PC_pres_i; instr_data_s[15:0] = instr_data_i;
  //   PC_fut_s[15:0] = PC_fut_o; PC_pres_incr_s[15:0] = LR_addr_o

  // Notes on the sheet:
  //   Attention, votre version de Logisim
  //   ne contient pas de tracker. Si vous
  //   enregistrez votre projet, toutes les
  //   informations du tracker seront
  //   définitivement effacées.
  //   Entité FETCH
  //   Increment du PC
  //   Control bus splitting
  //   Permet le saut
  //   L'état de PC va directement sur l'adresse d'instruction
endmodule

module condition_tester (
  input  cond_en_i,
  input  [3:0] cond_i,
  input  Z_i,
  input  C_i,
  input  N_i,
  input  V_i,
  output cond_test_o
);

  wire and_1_out, and_2_out, comparator_1_eq, not_1_out, not_2_out, not_3_out, not_4_out, not_5_out,
       not_6_out, not_7_out, not_8_out, or_1_out, or_2_out;
  wire [3:0] multiplexer_1_out;

  and and_1 (and_1_out, C_i, not_1_out);
  not not_1 (not_1_out, Z_i);
  not not_2 (not_2_out, C_i);
  or or_1 (or_1_out, not_2_out, Z_i);
  Comparator #(.width(1), .mode("unsigned")) comparator_1 (.a(N_i), .b(V_i), .eq(comparator_1_eq));  // open: gt, lt
  not not_3 (not_3_out, Z_i);
  not not_4 (not_4_out, comparator_1_eq);
  and and_2 (and_2_out, comparator_1_eq, not_3_out);
  or or_2 (or_2_out, not_4_out, Z_i);
  not not_5 (not_5_out, Z_i);
  not not_6 (not_6_out, C_i);
  not not_7 (not_7_out, N_i);
  not not_8 (not_8_out, V_i);
  Multiplexer #(.width(4), .enable("false")) multiplexer_1 (
    .in0(4'b1110), .in1(cond_i), .out(multiplexer_1_out), .sel(cond_en_i));
  Multiplexer #(.select(4), .enable("false")) multiplexer_2 (
    .in0(Z_i), .in1(not_5_out), .in2(C_i), .in3(not_6_out), .in4(N_i), .in5(not_7_out), .in6(V_i),
    .in7(not_8_out), .in8(and_1_out), .in9(or_1_out), .in10(comparator_1_eq), .in11(not_4_out),
    .in12(and_2_out), .in13(or_2_out), .in14(1'b1), .in15(1'b1), .out(cond_test_o), .sel(multiplexer_1_out));

  // Notes on the sheet:
  //   Attention, votre version de Logisim
  //   ne contient pas de tracker. Si vous
  //   enregistrez votre projet, toutes les
  //   informations du tracker seront
  //   définitivement effacées.
  //   Always (Inconditionnel)
endmodule

module decode (
  input  [15:0] instr_data_i,
  input  rst_i,
  input  clk_i,
  output [2:0] adr_reg_d_o,
  output [2:0] adr_reg_s_o,
  output [2:0] adr_reg_n_o,
  output [2:0] adr_reg_mem_o,
  output [2:0] imm3_o,
  output [4:0] imm5_o,
  output [10:0] offset11_o,
  output [7:0] offset8_o,
  output [7:0] imm8_o,
  output [1:0] reg_bank_control_bus_o,
  output [14:0] execute_control_bus_o,
  output [4:0] mem_control_bus_o,
  output [6:0] fetch_control_bus_o,
  output link_en_o,
  output fetch_en_o,
  output decode_en_o,
  output reg_bank_en_o,
  output execute_en_o,
  output memory_access_en_o
);

  wire or_1_out;
  wire [0:0] multiplexer_6_out;
  wire [1:0] comparator_1_eq, multiplexer_3_out, multiplexer_4_out;
  wire [2:0] rd_2_0_s, rd_10_8_s, rn_8_6_s, rs_5_3_s;
  wire [3:0] cond_s;
  wire [5:0] decode_control_bus_s;

  Multiplexer #(.width(3), .enable("false")) multiplexer_1 (
    .in0(rn_8_6_s), .in1(rs_5_3_s), .out(adr_reg_n_o), .sel(decode_control_bus_s[2]));
  Multiplexer #(.select(2), .width(3), .enable("false")) multiplexer_2 (
    .in0(rs_5_3_s), .in1(adr_reg_d_o), .in2(3'b111), .in3(3'b110), .out(adr_reg_s_o),
    .sel(decode_control_bus_s[1:0]));
  decode_instr_splitter Instr_Splitter_Inst (
    .instr_i(instr_data_i), .rd_2_0_o(rd_2_0_s), .rd_10_8_o(rd_10_8_s), .rs_5_3_o(rs_5_3_s),
    .rn_8_6_o(rn_8_6_s), .offset3_8_6_o(imm3_o), .offset5_10_6_o(imm5_o), .offset8_7_0_o(imm8_o),
    .offset11_10_0_o(offset11_o), .cond_11_8_o(cond_s));
  main_control_unit Control_Unit_Inst (
    .instr_i(instr_data_i), .cond_i(cond_s), .fetch_control_bus_o(fetch_control_bus_o),
    .decode_control_bus_o({decode_control_bus_s[5:4], link_en_o, decode_control_bus_s[2:0]}),
    .reg_bank_control_bus_o(reg_bank_control_bus_o), .execute_control_bus_o(execute_control_bus_o),
    .mem_control_bus_o(mem_control_bus_o), .fetch_en_o(fetch_en_o), .decode_en_o(decode_en_o),
    .reg_bank_en_o(reg_bank_en_o), .execute_en_o(execute_en_o), .memory_access_en_o(memory_access_en_o));
  Comparator #(.width(2)) comparator_1 (
    .a(decode_control_bus_s[1:0]), .b(2'b10), .eq(comparator_1_eq[0]));  // open: gt, lt
  Comparator #(.width(2)) comparator_2 (
    .a(decode_control_bus_s[1:0]), .b(2'b11), .eq(comparator_1_eq[1]));  // open: gt, lt
  Multiplexer #(.select(2), .width(2), .enable("false")) multiplexer_3 (
    .in0(2'b10), .in1(2'b10), .in2(2'b11), .in3(2'b11), .out(multiplexer_3_out), .sel(comparator_1_eq));
  or or_1 (or_1_out, comparator_1_eq[0], comparator_1_eq[1]);
  Multiplexer #(.width(2), .enable("false")) multiplexer_4 (
    .in0(2'b00), .in1(2'b01), .out(multiplexer_4_out), .sel(decode_control_bus_s[4]));
  Multiplexer #(.width(2), .enable("false")) multiplexer_5 (
    .in0(multiplexer_4_out), .in1(multiplexer_3_out), .sel(or_1_out));  // open: out
  Multiplexer #(.enable("false")) multiplexer_6 (
    .in0(decode_control_bus_s[4]), .in1(decode_control_bus_s[0]), .out(multiplexer_6_out[0]),
    .sel(decode_control_bus_s[1]));
  Multiplexer #(.select(2), .width(3), .enable("false")) multiplexer_7 (
    .in0(rd_2_0_s), .in1(rd_10_8_s), .in2(3'b110), .in3(3'b111), .out(adr_reg_d_o),
    .sel({decode_control_bus_s[1], multiplexer_6_out[0]}));

  assign adr_reg_mem_o = adr_reg_d_o;
  assign offset8_o = imm8_o;

  // Other names for the same wires on the sheet: sel_r_s[1:0] = decode_control_bus_s[1:0];
  //   adr_reg_d_s[2:0] = adr_reg_d_o; adr_reg_n_s[2:0] = adr_reg_n_o; adr_reg_s_s[2:0] = adr_reg_s_o;
  //   sel_r_n = decode_control_bus_s[2]; decode_control_bus_s[3] = link_en_o; link_en_s = link_en_o;
  //   sel_r_d = decode_control_bus_s[4]; offset3_8_6_s[2:0] = imm3_o; offset5_10_6_s[4:0] = imm5_o;
  //   offset8_7_0_s[7:0] = imm8_o; offset11_10_0_s[10:0] = offset11_o

  // Notes on the sheet:
  //   Attention, votre version de Logisim
  //   ne contient pas de tracker. Si vous
  //   enregistrez votre projet, toutes les
  //   informations du tracker seront
  //   définitivement effacées.
  //   Entité DECODE
  //   Splitter du bus de controle Decode :
  //   Selection d'adresse pour le registre source principale :
  //   Selection d'adresse pour le registre source secondaire :
  //   Selection d'adresse pour le registre destination :
endmodule

module decode_instr_splitter (
  input  [15:0] instr_i,
  output [2:0] rd_2_0_o,
  output [2:0] rd_10_8_o,
  output [2:0] rs_5_3_o,
  output [2:0] rn_8_6_o,
  output [2:0] offset3_8_6_o,
  output [4:0] offset5_10_6_o,
  output [7:0] offset8_7_0_o,
  output [10:0] offset11_10_0_o,
  output [3:0] cond_11_8_o
);


  assign cond_11_8_o = instr_i[11:8];
  assign offset3_8_6_o = instr_i[8:6];
  assign offset5_10_6_o = instr_i[10:6];
  assign offset8_7_0_o = instr_i[7:0];
  assign offset11_10_0_o = instr_i[10:0];
  assign rd_2_0_o = instr_i[2:0];
  assign rd_10_8_o = instr_i[10:8];
  assign rn_8_6_o = instr_i[8:6];
  assign rs_5_3_o = instr_i[5:3];

  // Notes on the sheet:
  //   Attention, votre version de Logisim
  //   ne contient pas de tracker. Si vous
  //   enregistrez votre projet, toutes les
  //   informations du tracker seront
  //   définitivement effacées.
endmodule

module main_control_unit (
  input  [15:0] instr_i,
  input  [3:0] cond_i,
  output [6:0] fetch_control_bus_o,
  output [5:0] decode_control_bus_o,
  output [1:0] reg_bank_control_bus_o,
  output [14:0] execute_control_bus_o,
  output [4:0] mem_control_bus_o,
  output fetch_en_o,
  output decode_en_o,
  output reg_bank_en_o,
  output execute_en_o,
  output memory_access_en_o
);

  wire add_r_imm_s, add_r_r_imm_s, add_r_r_r_s, and_r_r_s, asr_r_r_imm_s, asr_r_r_s, b_cond_s, b_incond_s,
       bl_lsb_s, bl_msb_s, byte_s, cond_en_s, eor_r_r_s, ldr_data_s, ldrb_r_r_imm_s, ldrb_r_r_r_s,
       ldrh_r_r_imm_s, ldrh_r_r_r_s, link_en_s, lsl_r_r_imm_s, lsl_r_r_s, lsr_r_r_imm_s, lsr_r_r_s,
       mov_r_imm_s, mvn_r_r_s, neg_r_r_s, orr_r_r_s, reg_bank_wr_s, ror_r_r_s, sel_cpsr_s, sel_mem_s,
       sel_operand_1_s, sel_PC_s, sel_rd_s, sel_rn_s, sel_shift_s, str_data_s, strb_r_r_imm_s, strb_r_r_r_s,
       strh_r_r_imm_s, strh_r_r_r_s, sub_r_imm_s, sub_r_r_imm_s, sub_r_r_r_s;
  wire [1:0] sel_operand_2_s, sel_rs_s;
  wire [2:0] sel_mult_2_s, sel_op_alu_s, sel_op_shift_s;

  opcode_supported_unit opcode_supported_unit_1 (
    .instr_i(instr_i), .lsl_r_r_imm_o(lsl_r_r_imm_s), .lsr_r_r_imm_o(lsr_r_r_imm_s),
    .asr_r_r_imm_o(asr_r_r_imm_s), .add_r_r_r_o(add_r_r_r_s), .add_r_r_imm_o(add_r_r_imm_s),
    .sub_r_r_r_o(sub_r_r_r_s), .sub_r_r_imm_o(sub_r_r_imm_s), .mov_r_imm_o(mov_r_imm_s),
    .add_r_imm_o(add_r_imm_s), .sub_r_imm_o(sub_r_imm_s), .and_r_r_o(and_r_r_s), .eor_r_r_o(eor_r_r_s),
    .lsl_r_r_o(lsl_r_r_s), .lsr_r_r_o(lsr_r_r_s), .asr_r_r_o(asr_r_r_s), .ror_r_r_o(ror_r_r_s),
    .neg_r_r_o(neg_r_r_s), .orr_r_r_o(orr_r_r_s), .mvn_r_r_o(mvn_r_r_s), .strb_r_r_r_o(strb_r_r_r_s),
    .ldrb_r_r_r_o(ldrb_r_r_r_s), .strh_r_r_r_o(strh_r_r_r_s), .ldrh_r_r_r_o(ldrh_r_r_r_s),
    .strb_r_r_imm_o(strb_r_r_imm_s), .ldrb_r_r_imm_o(ldrb_r_r_imm_s), .strh_r_r_imm_o(strh_r_r_imm_s),
    .ldrh_r_r_imm_o(ldrh_r_r_imm_s), .b_cond_o(b_cond_s), .b_incond_o(b_incond_s), .bl_msb_o(bl_msb_s),
    .bl_lsb_o(bl_lsb_s));
  fetch_control_unit fetch (
    .instr_i({1'b0, bl_lsb_s, bl_msb_s, b_incond_s, b_cond_s, ldrh_r_r_imm_s, strh_r_r_imm_s, ldrb_r_r_imm_s, strb_r_r_imm_s, ldrh_r_r_r_s, strh_r_r_r_s, ldrb_r_r_r_s, strb_r_r_r_s, mvn_r_r_s, orr_r_r_s, neg_r_r_s, ror_r_r_s, asr_r_r_s, lsr_r_r_s, lsl_r_r_s, eor_r_r_s, and_r_r_s, sub_r_imm_s, add_r_imm_s, mov_r_imm_s, sub_r_r_imm_s, sub_r_r_r_s, add_r_r_imm_s, add_r_r_r_s, asr_r_r_imm_s, lsr_r_r_imm_s, lsl_r_r_imm_s}),
    .sel_cpsr_o(sel_cpsr_s), .link_en_o(link_en_s), .sel_PC_o(sel_PC_s), .cond_en_o(cond_en_s));
  decode_control_unit decode (
    .instr_i({1'b0, bl_lsb_s, bl_msb_s, b_incond_s, b_cond_s, ldrh_r_r_imm_s, strh_r_r_imm_s, ldrb_r_r_imm_s, strb_r_r_imm_s, ldrh_r_r_r_s, strh_r_r_r_s, ldrb_r_r_r_s, strb_r_r_r_s, mvn_r_r_s, orr_r_r_s, neg_r_r_s, ror_r_r_s, asr_r_r_s, lsr_r_r_s, lsl_r_r_s, eor_r_r_s, and_r_r_s, sub_r_imm_s, add_r_imm_s, mov_r_imm_s, sub_r_r_imm_s, sub_r_r_r_s, add_r_r_imm_s, add_r_r_r_s, asr_r_r_imm_s, lsr_r_r_imm_s, lsl_r_r_imm_s}),
    .sel_rs_o(sel_rs_s), .sel_rn_o(sel_rn_s), .sel_rd_o(sel_rd_s));
  reg_bank_control_unit reg_bank (
    .instr_i({1'b0, bl_lsb_s, bl_msb_s, b_incond_s, b_cond_s, ldrh_r_r_imm_s, strh_r_r_imm_s, ldrb_r_r_imm_s, strb_r_r_imm_s, ldrh_r_r_r_s, strh_r_r_r_s, ldrb_r_r_r_s, strb_r_r_r_s, mvn_r_r_s, orr_r_r_s, neg_r_r_s, ror_r_r_s, asr_r_r_s, lsr_r_r_s, lsl_r_r_s, eor_r_r_s, and_r_r_s, sub_r_imm_s, add_r_imm_s, mov_r_imm_s, sub_r_r_imm_s, sub_r_r_r_s, add_r_r_imm_s, add_r_r_r_s, asr_r_r_imm_s, lsr_r_r_imm_s, lsl_r_r_imm_s}),
    .reg_bank_wr_o(reg_bank_wr_s));
  execute_control_unit execute (
    .instr_i({1'b0, bl_lsb_s, bl_msb_s, b_incond_s, b_cond_s, ldrh_r_r_imm_s, strh_r_r_imm_s, ldrb_r_r_imm_s, strb_r_r_imm_s, ldrh_r_r_r_s, strh_r_r_r_s, ldrb_r_r_r_s, strb_r_r_r_s, mvn_r_r_s, orr_r_r_s, neg_r_r_s, ror_r_r_s, asr_r_r_s, lsr_r_r_s, lsl_r_r_s, eor_r_r_s, and_r_r_s, sub_r_imm_s, add_r_imm_s, mov_r_imm_s, sub_r_r_imm_s, sub_r_r_r_s, add_r_r_imm_s, add_r_r_r_s, asr_r_r_imm_s, lsr_r_r_imm_s, lsl_r_r_imm_s}),
    .sel_operand_1_o(sel_operand_1_s), .sel_operand_2_o(sel_operand_2_s), .sel_op_shift_o(sel_op_shift_s),
    .sel_op_alu_o(sel_op_alu_s), .sel_mult_2_o(sel_mult_2_s), .sel_shift_o(sel_shift_s));
  memory_access_control_unit memory_acces (
    .instr_i({1'b0, bl_lsb_s, bl_msb_s, b_incond_s, b_cond_s, ldrh_r_r_imm_s, strh_r_r_imm_s, ldrb_r_r_imm_s, strb_r_r_imm_s, ldrh_r_r_r_s, strh_r_r_r_s, ldrb_r_r_r_s, strb_r_r_r_s, mvn_r_r_s, orr_r_r_s, neg_r_r_s, ror_r_r_s, asr_r_r_s, lsr_r_r_s, lsl_r_r_s, eor_r_r_s, and_r_r_s, sub_r_imm_s, add_r_imm_s, mov_r_imm_s, sub_r_r_imm_s, sub_r_r_r_s, add_r_r_imm_s, add_r_r_r_s, asr_r_r_imm_s, lsr_r_r_imm_s, lsl_r_r_imm_s}),
    .sel_mem_o(sel_mem_s), .str_data_o(str_data_s), .ldr_data_o(ldr_data_s), .byte_o(byte_s));
  bus_constructor bus_constructor_1 (
    .fetch_en_i(1'b0), .decode_en_i(1'b0), .reg_bank_en_i(1'b0), .execute_en_i(1'b0),
    .memory_access_en_i(1'b0), .cond_i(cond_i), .sel_cpsr_i(sel_cpsr_s), .link_en_i(link_en_s),
    .sel_PC_i(sel_PC_s), .cond_en_i(cond_en_s), .sel_rs_i(sel_rs_s), .sel_rn_i(sel_rn_s),
    .sel_rd_i(sel_rd_s), .reg_bank_wr_i(reg_bank_wr_s), .sel_operand_1_i(sel_operand_1_s),
    .sel_operand_2_i(sel_operand_2_s), .sel_op_shift_i(sel_op_shift_s), .sel_op_alu_i(sel_op_alu_s),
    .sel_mult_2_i(sel_mult_2_s), .sel_shift_i(sel_shift_s), .sel_mem_i(sel_mem_s), .str_data_i(str_data_s),
    .ldr_data_i(ldr_data_s), .byte_i(byte_s), .fetch_control_bus_o(fetch_control_bus_o),
    .decode_control_bus_o(decode_control_bus_o), .reg_bank_control_bus_o(reg_bank_control_bus_o),
    .execute_control_bus_o(execute_control_bus_o), .mem_control_bus_o(mem_control_bus_o));

  assign decode_en_o = 1'b1;
  assign execute_en_o = 1'b1;
  assign fetch_en_o = 1'b1;
  assign memory_access_en_o = 1'b1;
  assign reg_bank_en_o = 1'b1;

  // Other names for the same wires on the sheet: cond_s[3:0] = cond_i;
  //   decode_control_bus_s[5:0] = decode_control_bus_o; execute_control_bus_s[14:0] = execute_control_bus_o;
  //   fetch_control_bus_s[6:0] = fetch_control_bus_o; mem_control_bus_s[4:0] = mem_control_bus_o;
  //   reg_bank_control_bus_s[1:0] = reg_bank_control_bus_o

  // Notes on the sheet:
  //   Attention, votre version de Logisim
  //   ne contient pas de tracker. Si vous
  //   enregistrez votre projet, toutes les
  //   informations du tracker seront
  //   définitivement effacées.
endmodule

module opcode_supported_unit (
  input  [15:0] instr_i,
  output lsl_r_r_imm_o,
  output lsr_r_r_imm_o,
  output asr_r_r_imm_o,
  output add_r_r_r_o,
  output add_r_r_imm_o,
  output sub_r_r_r_o,
  output sub_r_r_imm_o,
  output mov_r_imm_o,
  output add_r_imm_o,
  output sub_r_imm_o,
  output and_r_r_o,
  output eor_r_r_o,
  output lsl_r_r_o,
  output lsr_r_r_o,
  output asr_r_r_o,
  output ror_r_r_o,
  output neg_r_r_o,
  output orr_r_r_o,
  output mvn_r_r_o,
  output strb_r_r_r_o,
  output ldrb_r_r_r_o,
  output strh_r_r_r_o,
  output ldrh_r_r_r_o,
  output strb_r_r_imm_o,
  output ldrb_r_r_imm_o,
  output strh_r_r_imm_o,
  output ldrh_r_r_imm_o,
  output b_cond_o,
  output b_incond_o,
  output bl_msb_o,
  output bl_lsb_o
);

  wire comparator_28_eq, comparator_29_eq;

  Comparator #(.width(5), .mode("unsigned")) comparator_1 (
    .a(instr_i[15:11]), .b({5{1'b0}}), .eq(lsl_r_r_imm_o));  // open: gt, lt
  Comparator #(.width(5), .mode("unsigned")) comparator_2 (
    .a(instr_i[15:11]), .b(5'b00001), .eq(lsr_r_r_imm_o));  // open: gt, lt
  Comparator #(.width(5), .mode("unsigned")) comparator_3 (
    .a(instr_i[15:11]), .b(5'b00010), .eq(asr_r_r_imm_o));  // open: gt, lt
  Comparator #(.width(7), .mode("unsigned")) comparator_4 (
    .a(instr_i[15:9]), .b(7'b0001100), .eq(add_r_r_r_o));  // open: gt, lt
  Comparator #(.width(7), .mode("unsigned")) comparator_5 (
    .a(instr_i[15:9]), .b(7'b0001110), .eq(add_r_r_imm_o));  // open: gt, lt
  Comparator #(.width(7), .mode("unsigned")) comparator_6 (
    .a(instr_i[15:9]), .b(7'b0001101), .eq(sub_r_r_r_o));  // open: gt, lt
  Comparator #(.width(7), .mode("unsigned")) comparator_7 (
    .a(instr_i[15:9]), .b(7'b0001111), .eq(sub_r_r_imm_o));  // open: gt, lt
  Comparator #(.width(5), .mode("unsigned")) comparator_8 (
    .a(instr_i[15:11]), .b(5'b00100), .eq(mov_r_imm_o));  // open: gt, lt
  Comparator #(.width(5), .mode("unsigned")) comparator_9 (
    .a(instr_i[15:11]), .b(5'b00110), .eq(add_r_imm_o));  // open: gt, lt
  Comparator #(.width(5), .mode("unsigned")) comparator_10 (
    .a(instr_i[15:11]), .b(5'b00111), .eq(sub_r_imm_o));  // open: gt, lt
  Comparator #(.width(10), .mode("unsigned")) comparator_11 (
    .a(instr_i[15:6]), .b(10'h100), .eq(and_r_r_o));  // open: gt, lt
  Comparator #(.width(10), .mode("unsigned")) comparator_12 (
    .a(instr_i[15:6]), .b(10'h101), .eq(eor_r_r_o));  // open: gt, lt
  Comparator #(.width(10), .mode("unsigned")) comparator_13 (
    .a(instr_i[15:6]), .b(10'h102), .eq(lsl_r_r_o));  // open: gt, lt
  Comparator #(.width(10), .mode("unsigned")) comparator_14 (
    .a(instr_i[15:6]), .b(10'h103), .eq(lsr_r_r_o));  // open: gt, lt
  Comparator #(.width(10), .mode("unsigned")) comparator_15 (
    .a(instr_i[15:6]), .b(10'h104), .eq(asr_r_r_o));  // open: gt, lt
  Comparator #(.width(10), .mode("unsigned")) comparator_16 (
    .a(instr_i[15:6]), .b(10'h107), .eq(ror_r_r_o));  // open: gt, lt
  Comparator #(.width(10), .mode("unsigned")) comparator_17 (
    .a(instr_i[15:6]), .b(10'h109), .eq(neg_r_r_o));  // open: gt, lt
  Comparator #(.width(10), .mode("unsigned")) comparator_18 (
    .a(instr_i[15:6]), .b(10'h10c), .eq(orr_r_r_o));  // open: gt, lt
  Comparator #(.width(10), .mode("unsigned")) comparator_19 (
    .a(instr_i[15:6]), .b(10'h10f), .eq(mvn_r_r_o));  // open: gt, lt
  Comparator #(.width(7), .mode("unsigned")) comparator_20 (
    .a(instr_i[15:9]), .b(7'b0101010), .eq(strb_r_r_r_o));  // open: gt, lt
  Comparator #(.width(7), .mode("unsigned")) comparator_21 (
    .a(instr_i[15:9]), .b(7'b0101110), .eq(ldrb_r_r_r_o));  // open: gt, lt
  Comparator #(.width(7), .mode("unsigned")) comparator_22 (
    .a(instr_i[15:9]), .b(7'b0101001), .eq(strh_r_r_r_o));  // open: gt, lt
  Comparator #(.width(7), .mode("unsigned")) comparator_23 (
    .a(instr_i[15:9]), .b(7'b0101101), .eq(ldrh_r_r_r_o));  // open: gt, lt
  Comparator #(.width(5), .mode("unsigned")) comparator_24 (
    .a(instr_i[15:11]), .b(5'b01110), .eq(strb_r_r_imm_o));  // open: gt, lt
  Comparator #(.width(5), .mode("unsigned")) comparator_25 (
    .a(instr_i[15:11]), .b(5'b01111), .eq(ldrb_r_r_imm_o));  // open: gt, lt
  Comparator #(.width(5), .mode("unsigned")) comparator_26 (
    .a(instr_i[15:11]), .b(5'b10000), .eq(strh_r_r_imm_o));  // open: gt, lt
  Comparator #(.width(5), .mode("unsigned")) comparator_27 (
    .a(instr_i[15:11]), .b(5'b10001), .eq(ldrh_r_r_imm_o));  // open: gt, lt
  Comparator #(.width(4), .mode("unsigned")) comparator_28 (
    .a(instr_i[15:12]), .b(4'b1101), .eq(comparator_28_eq));  // open: gt, lt
  Comparator #(.width(4), .mode("unsigned")) comparator_29 (
    .a(instr_i[11:8]), .b(4'b1111), .eq(comparator_29_eq));  // open: gt, lt
  Comparator #(.width(5), .mode("unsigned")) comparator_30 (
    .a(instr_i[15:11]), .b(5'b11100), .eq(b_incond_o));  // open: gt, lt
  Comparator #(.width(5), .mode("unsigned")) comparator_31 (
    .a(instr_i[15:11]), .b(5'b11110), .eq(bl_msb_o));  // open: gt, lt
  Comparator #(.width(5), .mode("unsigned")) comparator_32 (
    .a(instr_i[15:11]), .b({5{1'b1}}), .eq(bl_lsb_o));  // open: gt, lt
  and and_1 (b_cond_o, comparator_28_eq, ~comparator_29_eq);  // AND_Gate

  // Other names for the same wires on the sheet: add_r_imm = add_r_imm_o; add_r_r_imm = add_r_r_imm_o;
  //   add_r_r_r = add_r_r_r_o; and_r_r = and_r_r_o; asr_r_r = asr_r_r_o; asr_r_r_imm = asr_r_r_imm_o;
  //   b_cond = b_cond_o; b_incond = b_incond_o; bl_lsb = bl_lsb_o; bl_msb = bl_msb_o; eor_r_r = eor_r_r_o;
  //   ldrb_r_r_imm = ldrb_r_r_imm_o; ldrb_r_r_r = ldrb_r_r_r_o; ldrh_r_r_imm = ldrh_r_r_imm_o;
  //   ldrh_r_r_r = ldrh_r_r_r_o; lsl_r_r = lsl_r_r_o; lsl_r_r_imm = lsl_r_r_imm_o; lsr_r_r = lsr_r_r_o;
  //   lsr_r_r_imm = lsr_r_r_imm_o; mov_r_imm = mov_r_imm_o; mvn_r_r = mvn_r_r_o; neg_r_r = neg_r_r_o;
  //   orr_r_r = orr_r_r_o; ror_r_r = ror_r_r_o; strb_r_r_imm = strb_r_r_imm_o; strb_r_r_r = strb_r_r_r_o;
  //   strh_r_r_imm = strh_r_r_imm_o; strh_r_r_r = strh_r_r_r_o; sub_r_imm = sub_r_imm_o; sub_r_r_imm = sub_r_r_imm_o;
  //   sub_r_r_r = sub_r_r_r_o

  // Notes on the sheet:
  //   Attention, votre version de Logisim
  //   ne contient pas de tracker. Si vous
  //   enregistrez votre projet, toutes les
  //   informations du tracker seront
  //   définitivement effacées.
  //   Extraction des instructions supportées
  //   0101010
  //   0101110
  //   0101001
  //   0101011
  //   01101
  //   01111
  //   10000
  //   10001
endmodule

module fetch_control_unit (
  input  [31:0] instr_i,
  output sel_cpsr_o,
  output link_en_o,
  output sel_PC_o,
  output cond_en_o
);

  or or_1 (sel_PC_o, instr_i[27], instr_i[28], instr_i[30]);
  nor nor_1 (sel_cpsr_o, instr_i[19], instr_i[20], instr_i[21], instr_i[22], instr_i[23], instr_i[24], instr_i[25], instr_i[26], instr_i[27], instr_i[28], instr_i[29], instr_i[30]);

  assign cond_en_o = instr_i[27];
  assign link_en_o = instr_i[29];

  // Other names for the same wires on the sheet: lsl_r_r_imm_s = instr_i[0]; lsr_r_r_imm_s = instr_i[1];
  //   asr_r_r_imm_s = instr_i[2]; add_r_r_r_s = instr_i[3]; add_r_r_imm_s = instr_i[4]; sub_r_r_r_s = instr_i[5];
  //   sub_r_r_imm_s = instr_i[6]; mov_r_imm_s = instr_i[7]; add_r_imm_s = instr_i[8]; sub_r_imm_s = instr_i[9];
  //   and_r_r_s = instr_i[10]; eor_r_r_s = instr_i[11]; lsl_r_r_s = instr_i[12]; lsr_r_r_s = instr_i[13];
  //   asr_r_r_s = instr_i[14]; ror_r_r_s = instr_i[15]; neg_r_r_s = instr_i[16]; orr_r_r_s = instr_i[17];
  //   mvn_r_r_s = instr_i[18]; strb_r_r_r_s = instr_i[19]; ldrb_r_r_r_s = instr_i[20]; strh_r_r_r_s = instr_i[21];
  //   ldrh_r_r_r_s = instr_i[22]; strb_r_r_imm_s = instr_i[23]; ldrb_r_r_imm_s = instr_i[24];
  //   strh_r_r_imm_s = instr_i[25]; ldrh_r_r_imm_s = instr_i[26]; b_cond_s = instr_i[27]; cond_en_s = instr_i[27];
  //   b_incond_s = instr_i[28]; bl_msb_s = instr_i[29]; link_en_s = instr_i[29]; bl_lsb_s = instr_i[30];
  //   sel_cpsr_s = sel_cpsr_o; sel_PC_s = sel_PC_o

  // Notes on the sheet:
  //   Attention, votre version de Logisim
  //   ne contient pas de tracker. Si vous
  //   enregistrez votre projet, toutes les
  //   informations du tracker seront
  //   définitivement effacées.
endmodule

module decode_control_unit (
  input  [31:0] instr_i,
  output [1:0] sel_rs_o,
  output sel_rn_o,
  output sel_rd_o
);

  or or_1 (sel_rs_o[1], instr_i[27], instr_i[28], instr_i[29], instr_i[30]);
  or or_2 (sel_rs_o[0], instr_i[8], instr_i[9], instr_i[10], instr_i[11], instr_i[12], instr_i[14], instr_i[15], instr_i[17], instr_i[30], instr_i[13]);
  or or_3 (sel_rn_o, instr_i[10], instr_i[11], instr_i[12], instr_i[13], instr_i[14], instr_i[15], instr_i[17]);
  or or_4 (sel_rd_o, instr_i[7], instr_i[8], instr_i[9]);

  // Other names for the same wires on the sheet: lsl_r_r_imm_s = instr_i[0]; lsr_r_r_imm_s = instr_i[1];
  //   asr_r_r_imm_s = instr_i[2]; add_r_r_r_s = instr_i[3]; add_r_r_imm_s = instr_i[4]; sub_r_r_r_s = instr_i[5];
  //   sub_r_r_imm_s = instr_i[6]; mov_r_imm_s = instr_i[7]; add_r_imm_s = instr_i[8]; sub_r_imm_s = instr_i[9];
  //   and_r_r_s = instr_i[10]; eor_r_r_s = instr_i[11]; lsl_r_r_s = instr_i[12]; lsr_r_r_s = instr_i[13];
  //   asr_r_r_s = instr_i[14]; ror_r_r_s = instr_i[15]; neg_r_r_s = instr_i[16]; orr_r_r_s = instr_i[17];
  //   mvn_r_r_s = instr_i[18]; strb_r_r_r_s = instr_i[19]; ldrb_r_r_r_s = instr_i[20]; strh_r_r_r_s = instr_i[21];
  //   ldrh_r_r_r_s = instr_i[22]; strb_r_r_imm_s = instr_i[23]; ldrb_r_r_imm_s = instr_i[24];
  //   strh_r_r_imm_s = instr_i[25]; ldrh_r_r_imm_s = instr_i[26]; b_cond_s = instr_i[27]; b_incond_s = instr_i[28];
  //   bl_msb_s = instr_i[29]; bl_lsb_s = instr_i[30]; sel_rd_s = sel_rd_o; sel_rn_s = sel_rn_o;
  //   sel_rs_s[1:0] = sel_rs_o

  // Notes on the sheet:
  //   Attention, votre version de Logisim
  //   ne contient pas de tracker. Si vous
  //   enregistrez votre projet, toutes les
  //   informations du tracker seront
  //   définitivement effacées.
endmodule

module reg_bank_control_unit (
  input  [31:0] instr_i,
  output reg_bank_wr_o
);

  nor nor_1 (reg_bank_wr_o, instr_i[19], instr_i[21], instr_i[23], instr_i[25], instr_i[27], instr_i[28]);

  // Other names for the same wires on the sheet: lsl_r_r_imm_s = instr_i[0]; lsr_r_r_imm_s = instr_i[1];
  //   asr_r_r_imm_s = instr_i[2]; add_r_r_r_s = instr_i[3]; add_r_r_imm_s = instr_i[4]; sub_r_r_r_s = instr_i[5];
  //   sub_r_r_imm_s = instr_i[6]; mov_r_imm_s = instr_i[7]; add_r_imm_s = instr_i[8]; sub_r_imm_s = instr_i[9];
  //   and_r_r_s = instr_i[10]; eor_r_r_s = instr_i[11]; lsl_r_r_s = instr_i[12]; lsr_r_r_s = instr_i[13];
  //   asr_r_r_s = instr_i[14]; ror_r_r_s = instr_i[15]; neg_r_r_s = instr_i[16]; orr_r_r_s = instr_i[17];
  //   mvn_r_r_s = instr_i[18]; strb_r_r_r_s = instr_i[19]; ldrb_r_r_r_s = instr_i[20]; strh_r_r_r_s = instr_i[21];
  //   ldrh_r_r_r_s = instr_i[22]; strb_r_r_imm_s = instr_i[23]; ldrb_r_r_imm_s = instr_i[24];
  //   strh_r_r_imm_s = instr_i[25]; ldrh_r_r_imm_s = instr_i[26]; b_cond_s = instr_i[27]; b_incond_s = instr_i[28];
  //   bl_msb_s = instr_i[29]; bl_lsb_s = instr_i[30]; reg_bank_wr_s = reg_bank_wr_o

  // Notes on the sheet:
  //   Attention, votre version de Logisim
  //   ne contient pas de tracker. Si vous
  //   enregistrez votre projet, toutes les
  //   informations du tracker seront
  //   définitivement effacées.
endmodule

module execute_control_unit (
  input  [31:0] instr_i,
  output sel_operand_1_o,
  output [1:0] sel_operand_2_o,
  output [2:0] sel_op_shift_o,
  output [2:0] sel_op_alu_o,
  output [2:0] sel_mult_2_o,
  output sel_shift_o
);

  wire or_1_out;

  or or_1 (or_1_out, instr_i[7], instr_i[8], instr_i[9]);
  or or_2 (sel_op_shift_o[0], instr_i[1], instr_i[13], instr_i[2], instr_i[14]);
  or or_3 (sel_op_shift_o[1], instr_i[0], instr_i[1], instr_i[12], instr_i[13]);
  or or_4 (sel_op_alu_o[1], instr_i[5], instr_i[6], instr_i[9], instr_i[10], instr_i[11], instr_i[16]);
  or or_5 (sel_op_alu_o[2], instr_i[11], instr_i[16], instr_i[17], instr_i[18]);
  or or_6 (sel_mult_2_o[0], instr_i[29], instr_i[28], instr_i[30]);
  or or_7 (sel_mult_2_o[1], instr_i[30], instr_i[27]);
  or or_8 (sel_mult_2_o[2], instr_i[19], instr_i[23], instr_i[20], instr_i[24], instr_i[29]);
  or or_9 (sel_operand_2_o[0], instr_i[4], instr_i[6], or_1_out);
  or or_10 (sel_op_alu_o[0], instr_i[27], instr_i[28], instr_i[29], instr_i[30], instr_i[3], instr_i[4], instr_i[7], instr_i[8], instr_i[10], instr_i[11], instr_i[18], instr_i[19], instr_i[20], instr_i[21], instr_i[22], instr_i[23], instr_i[24], instr_i[25], instr_i[26]);
  or or_11 (sel_shift_o, instr_i[12], instr_i[13], instr_i[14], instr_i[15]);
  or or_12 (sel_operand_2_o[1], instr_i[23], instr_i[24], instr_i[25], instr_i[26], instr_i[27], instr_i[28], instr_i[29], instr_i[30]);

  assign sel_op_shift_o[2] = instr_i[15];
  assign sel_operand_1_o = instr_i[7];

  // Other names for the same wires on the sheet: lsl_r_r_imm_s = instr_i[0]; lsr_r_r_imm_s = instr_i[1];
  //   asr_r_r_imm_s = instr_i[2]; add_r_r_r_s = instr_i[3]; add_r_r_imm_s = instr_i[4]; sub_r_r_r_s = instr_i[5];
  //   sub_r_r_imm_s = instr_i[6]; mov_r_imm_s = instr_i[7]; sel_operand_1_s = instr_i[7]; add_r_imm_s = instr_i[8];
  //   sub_r_imm_s = instr_i[9]; and_r_r_s = instr_i[10]; eor_r_r_s = instr_i[11]; lsl_r_r_s = instr_i[12];
  //   lsr_r_r_s = instr_i[13]; asr_r_r_s = instr_i[14]; neg_r_r_s = instr_i[16]; orr_r_r_s = instr_i[17];
  //   mvn_r_r_s = instr_i[18]; strb_r_r_r_s = instr_i[19]; ldrb_r_r_r_s = instr_i[20]; strh_r_r_r_s = instr_i[21];
  //   ldrh_r_r_r_s = instr_i[22]; strb_r_r_imm_s = instr_i[23]; ldrb_r_r_imm_s = instr_i[24];
  //   strh_r_r_imm_s = instr_i[25]; ldrh_r_r_imm_s = instr_i[26]; b_cond_s = instr_i[27]; b_incond_s = instr_i[28];
  //   bl_msb_s = instr_i[29]; bl_lsb_s = instr_i[30]; sel_mult_2_s[2:0] = sel_mult_2_o;
  //   sel_op_alu_0_s = sel_op_alu_o[0]; sel_op_alu_s[2:0] = sel_op_alu_o; sel_op_alu_1_s = sel_op_alu_o[1];
  //   sel_op_alu_2_s = sel_op_alu_o[2]; sel_op_shift_0_s = sel_op_shift_o[0];
  //   sel_op_shift_s[2:0] = {instr_i[15], sel_op_shift_o[1:0]}; sel_op_shift_1_s = sel_op_shift_o[1];
  //   ror_r_r_s = instr_i[15]; sel_op_shift_2_s = instr_i[15]; sel_operand_2_s[1:0] = sel_operand_2_o;
  //   sel_shift_s = sel_shift_o

  // Notes on the sheet:
  //   Attention, votre version de Logisim
  //   ne contient pas de tracker. Si vous
  //   enregistrez votre projet, toutes les
  //   informations du tracker seront
  //   définitivement effacées.
  //   sel_operand_1
  //   sel_operand_2
  //   sel_op_shift
  //   sel_op_alu
  //   sel_mult_2
  //   sel_shift
endmodule

module memory_access_control_unit (
  input  [31:0] instr_i,
  output sel_mem_o,
  output str_data_o,
  output ldr_data_o,
  output byte_o
);

  or or_1 (sel_mem_o, instr_i[19], instr_i[20], instr_i[21], instr_i[22], instr_i[23], instr_i[24], instr_i[25], instr_i[26]);
  or or_2 (str_data_o, instr_i[19], instr_i[21], instr_i[23], instr_i[25]);
  or or_3 (ldr_data_o, instr_i[20], instr_i[22], instr_i[24], instr_i[26]);
  or or_4 (byte_o, instr_i[19], instr_i[20], instr_i[25], instr_i[26]);

  // Other names for the same wires on the sheet: byte_s = byte_o; lsl_r_r_imm_s = instr_i[0];
  //   lsr_r_r_imm_s = instr_i[1]; asr_r_r_imm_s = instr_i[2]; add_r_r_r_s = instr_i[3]; add_r_r_imm_s = instr_i[4];
  //   sub_r_r_r_s = instr_i[5]; sub_r_r_imm_s = instr_i[6]; mov_r_imm_s = instr_i[7]; add_r_imm_s = instr_i[8];
  //   sub_r_imm_s = instr_i[9]; and_r_r_s = instr_i[10]; eor_r_r_s = instr_i[11]; lsl_r_r_s = instr_i[12];
  //   lsr_r_r_s = instr_i[13]; asr_r_r_s = instr_i[14]; ror_r_r_s = instr_i[15]; neg_r_r_s = instr_i[16];
  //   orr_r_r_s = instr_i[17]; mvn_r_r_s = instr_i[18]; strb_r_r_r_s = instr_i[19]; ldrb_r_r_r_s = instr_i[20];
  //   strh_r_r_r_s = instr_i[21]; ldrh_r_r_r_s = instr_i[22]; strb_r_r_imm_s = instr_i[23];
  //   ldrb_r_r_imm_s = instr_i[24]; strh_r_r_imm_s = instr_i[25]; ldrh_r_r_imm_s = instr_i[26];
  //   b_cond_s = instr_i[27]; b_incond_s = instr_i[28]; bl_msb_s = instr_i[29]; bl_lsb_s = instr_i[30];
  //   ldr_data_s = ldr_data_o; sel_mem_s = sel_mem_o; str_data_s = str_data_o

  // Notes on the sheet:
  //   Attention, votre version de Logisim
  //   ne contient pas de tracker. Si vous
  //   enregistrez votre projet, toutes les
  //   informations du tracker seront
  //   définitivement effacées.
endmodule

module bus_constructor (
  input  fetch_en_i,
  input  decode_en_i,
  input  reg_bank_en_i,
  input  execute_en_i,
  input  memory_access_en_i,
  input  [3:0] cond_i,
  input  sel_cpsr_i,
  input  link_en_i,
  input  sel_PC_i,
  input  cond_en_i,
  input  [1:0] sel_rs_i,
  input  sel_rn_i,
  input  sel_rd_i,
  input  reg_bank_wr_i,
  input  sel_operand_1_i,
  input  [1:0] sel_operand_2_i,
  input  [2:0] sel_op_shift_i,
  input  [2:0] sel_op_alu_i,
  input  [2:0] sel_mult_2_i,
  input  sel_shift_i,
  input  sel_mem_i,
  input  str_data_i,
  input  ldr_data_i,
  input  byte_i,
  output [6:0] fetch_control_bus_o,
  output [5:0] decode_control_bus_o,
  output [1:0] reg_bank_control_bus_o,
  output [14:0] execute_control_bus_o,
  output [4:0] mem_control_bus_o
);


  assign decode_control_bus_o = {1'b0, sel_rd_i, link_en_i, sel_rn_i, sel_rs_i};
  assign execute_control_bus_o = {1'b0, sel_mult_2_i, sel_cpsr_i, sel_shift_i, sel_operand_1_i, sel_operand_2_i, sel_op_alu_i, sel_op_shift_i};
  assign fetch_control_bus_o = {1'b0, cond_i, cond_en_i, sel_PC_i};
  assign mem_control_bus_o = {1'b0, byte_i, ldr_data_i, str_data_i, sel_mem_i};
  assign reg_bank_control_bus_o = {reg_bank_wr_i, 1'b0};

  // Other names for the same wires on the sheet: decode_control_bus_s[4:0] = {sel_rd_i, link_en_i, sel_rn_i, sel_rs_i};
  //   sel_rs_s[1:0] = sel_rs_i; sel_rn_s = sel_rn_i; link_en_s = link_en_i; sel_rd_s = sel_rd_i;
  //   decode_en_s = decode_en_i;
  //   execute_control_bus_s[13:0] = {sel_mult_2_i, sel_cpsr_i, sel_shift_i, sel_operand_1_i, sel_operand_2_i, sel_op_alu_i, sel_op_shift_i};
  //   sel_op_shift_s[2:0] = sel_op_shift_i; sel_op_alu_s[2:0] = sel_op_alu_i; sel_operand_2_s[1:0] = sel_operand_2_i;
  //   sel_operand_1_s = sel_operand_1_i; sel_shift_s = sel_shift_i; sel_cpsr_s = sel_cpsr_i;
  //   sel_mult_2_s[2:0] = sel_mult_2_i; execute_en_s = execute_en_i;
  //   fetch_control_bus_s[5:0] = {cond_i, cond_en_i, sel_PC_i}; sel_PC_s = sel_PC_i; cond_en_s = cond_en_i;
  //   cond_s[3:0] = cond_i; fetch_en_s = fetch_en_i;
  //   mem_control_bus_s[3:0] = {byte_i, ldr_data_i, str_data_i, sel_mem_i}; sel_mem_s = sel_mem_i;
  //   str_data_s = str_data_i; ldr_data_s = ldr_data_i; byte_s = byte_i; memory_access_en_s = memory_access_en_i;
  //   reg_bank_control_bus_s[1] = reg_bank_wr_i; reg_bank_wr_s = reg_bank_wr_i; reg_bank_en_s = reg_bank_en_i

  // Notes on the sheet:
  //   Attention, votre version de Logisim
  //   ne contient pas de tracker. Si vous
  //   enregistrez votre projet, toutes les
  //   informations du tracker seront
  //   définitivement effacées.
endmodule

module bank_registers (
  input  clk_i,
  input  rst_i,
  input  [2:0] register_d_sel_i,
  input  [15:0] register_d_data_i,
  input  [2:0] register_s_sel_i,
  input  [2:0] register_n_sel_i,
  input  [2:0] register_mem_sel_i,
  input  [1:0] reg_bank_control_bus_i,
  input  [15:0] PC_fut_i,
  input  [15:0] LR_addr_i,
  input  branch_i,
  input  link_en_i,
  input  reg_bank_en_i,
  output [15:0] register_s_read_data_o,
  output [15:0] register_n_read_data_o,
  output [15:0] register_mem_read_data_o,
  output [15:0] PC_pres_o
);

  wire and_1_out, and_2_out, LR, LR_wr_en_o, not_1_out, R0, R1, R2, R3, R4, SP, write_en_PC;
  wire [15:0] LR_data_o, LR_o, PC_data_o, R0_o, R1_o, R2_o, R3_o, R4_o, SP_o;

  Register #(.width(16)) u_R0 (.D(register_d_data_i), .en(R0), .clk(clk_i), .Q(R0_o), .clr(rst_i));
  Register #(.width(16)) u_R4 (.D(register_d_data_i), .en(R4), .clk(clk_i), .Q(R4_o), .clr(rst_i));
  Multiplexer #(.select(3), .width(16), .enable("false")) multiplexer_1 (
    .in0(R0_o), .in1(R1_o), .in2(R2_o), .in3(R3_o), .in4(R4_o), .in5(SP_o), .in6(LR_o), .in7(PC_pres_o),
    .out(register_s_read_data_o), .sel(register_s_sel_i));
  Multiplexer #(.select(3), .width(16), .enable("false")) multiplexer_2 (
    .in0(R0_o), .in1(R1_o), .in2(R2_o), .in3(R3_o), .in4(R4_o), .in5(SP_o), .in6(LR_o), .in7(PC_pres_o),
    .out(register_n_read_data_o), .sel(register_n_sel_i));
  Multiplexer #(.select(3), .width(16), .enable("false")) multiplexer_3 (
    .in0(R0_o), .in1(R1_o), .in2(R2_o), .in3(R3_o), .in4(R4_o), .in5(SP_o), .in6(LR_o), .in7(PC_pres_o),
    .out(register_mem_read_data_o), .sel(register_mem_sel_i));
  Register #(.width(16)) u_R1 (.D(register_d_data_i), .en(R1), .clk(clk_i), .Q(R1_o), .clr(rst_i));
  Register #(.width(16)) u_SP (.D(register_d_data_i), .en(SP), .clk(clk_i), .Q(SP_o), .clr(rst_i));
  Register #(.width(16)) u_R2 (.D(register_d_data_i), .en(R2), .clk(clk_i), .Q(R2_o), .clr(rst_i));
  Register #(.width(16)) u_LR (.D(LR_data_o), .en(LR_wr_en_o), .clk(clk_i), .Q(LR_o), .clr(rst_i));
  and and_1 (and_1_out, write_en_PC, not_1_out);
  not not_1 (not_1_out, link_en_i);
  Multiplexer #(.width(16), .enable("false")) multiplexer_4 (
    .in0(PC_fut_i), .in1(register_d_data_i), .out(PC_data_o), .sel(and_1_out));
  Register #(.width(16)) u_R3 (.D(register_d_data_i), .en(R3), .clk(clk_i), .Q(R3_o), .clr(rst_i));
  Register #(.width(16)) PC (.D(PC_data_o), .en(1'b1), .clk(clk_i), .Q(PC_pres_o), .clr(rst_i));
  LR_manager lr_manager_1 (
    .data_i(register_d_data_i), .pc_fut_lr_i(PC_fut_i), .LR_addr_i(LR_addr_i), .branch_i(branch_i),
    .write_en_i(LR), .link_en_i(link_en_i), .clk_i(clk_i), .rst_i(rst_i), .LR_data_o(LR_data_o),
    .LR_wr_en_o(LR_wr_en_o));
  and and_2 (and_2_out, reg_bank_en_i, reg_bank_control_bus_i[1]);
  Decoder #(.select(3)) decoder_1 (
    .out0(R0), .out1(R1), .out2(R2), .out3(R3), .out4(R4), .out5(SP), .out6(LR), .out7(write_en_PC),
    .sel(register_d_sel_i), .en(and_2_out));

  // Other names for the same wires on the sheet: branch_s = branch_i; clk_s = clk_i; link_en_s = link_en_i;
  //   LR_addr_s[15:0] = LR_addr_i; PC_fut_s[15:0] = PC_fut_i; PC_o[15:0] = PC_pres_o; PC_pres[15:0] = PC_pres_o;
  //   reg_bank_control_bus[1:0] = reg_bank_control_bus_i; reg_bank_en_s = reg_bank_en_i;
  //   reg_d_sel_s[2:0] = register_d_sel_i; reg_mem_read_data_s[15:0] = register_mem_read_data_o;
  //   reg_mem_sel_s[2:0] = register_mem_sel_i; reg_n_read_data_s[15:0] = register_n_read_data_o;
  //   reg_n_sel_s[2:0] = register_n_sel_i; reg_s_read_data_s[15:0] = register_s_read_data_o;
  //   reg_s_sel_s[2:0] = register_s_sel_i; reg_write_data_s[15:0] = register_d_data_i; rst_s = rst_i

  // Notes on the sheet:
  //   Attention, votre version de Logisim
  //   ne contient pas de tracker. Si vous
  //   enregistrez votre projet, toutes les
  //   informations du tracker seront
  //   définitivement effacées.
  //   Banque de registres
  //   Banque de registre :
  //   Sélection des registres de lecture (source) :
  //   Sélecteur (enables) des données pour le PC :
  //   Management du LR :
  //   Enable de la banque de registres
  //   Sélection du registre de destination
endmodule

module LR_manager (
  input  [15:0] data_i,
  input  [15:0] pc_fut_lr_i,
  input  [15:0] LR_addr_i,
  input  branch_i,
  input  write_en_i,
  input  link_en_i,
  input  clk_i,
  input  rst_i,
  output [15:0] LR_data_o,
  output LR_wr_en_o
);

  wire and_1_out, link_en_d1_s, or_1_out;
  wire [15:0] multiplexer_1_out;

  Multiplexer #(.width(16), .enable("false")) multiplexer_1 (
    .in0(data_i), .in1(pc_fut_lr_i), .out(multiplexer_1_out), .sel(and_1_out));
  and and_1 (and_1_out, branch_i, link_en_i);
  D_Flip_Flop d_ff_1 (.D(link_en_i), .clk(clk_i), .Q(link_en_d1_s), .preset(1'b0), .reset(rst_i));  // open: Qn
  or or_1 (or_1_out, write_en_i, link_en_i);
  Multiplexer #(.width(16), .enable("false")) multiplexer_2 (
    .in0(multiplexer_1_out), .in1(LR_addr_i), .out(LR_data_o), .sel(link_en_d1_s));
  or or_2 (LR_wr_en_o, or_1_out, link_en_d1_s);

  // Other names for the same wires on the sheet: clk_s = clk_i; link_en_s = link_en_i; rst_s = rst_i

  // Notes on the sheet:
  //   Attention, votre version de Logisim
  //   ne contient pas de tracker. Si vous
  //   enregistrez votre projet, toutes les
  //   informations du tracker seront
  //   définitivement effacées.
endmodule

module execute (
  input  [15:0] reg_data_s_i,
  input  [15:0] reg_data_n_i,
  input  [2:0] imm3,
  input  [4:0] imm5,
  input  [10:0] offset_incond,
  input  [7:0] offset_cond,
  input  [7:0] imm8,
  input  [14:0] execute_control_bus,
  input  rst_i,
  input  clk_i,
  input  execute_en_i,
  output [15:0] data_out_o,
  output [3:0] cpsr_o
);

  wire carry_s, overflow_s;
  wire [3:0] reg_data_m_s, sel_shift_data_s, zcnv_unit_1_z_o;
  wire [15:0] bit_extender_1_out, mult_2_out_s, operand_1_s, operand_2_s, shift_1_shift_data_out_o;

  assign bit_extender_1_out = {{8{1'b0}}, imm8};  // Bit_Extender bit_extender_1
  Multiplexer #(.select(2), .width(16), .enable("false")) multiplexer_1 (
    .in0(reg_data_n_i), .in1({{13{1'b0}}, imm3}), .in2(mult_2_out_s), .in3(bit_extender_1_out),
    .out(operand_2_s), .sel(execute_control_bus[7:6]));
  Multiplexer #(.width(16), .enable("false")) multiplexer_2 (
    .in0(reg_data_s_i), .in1({16{1'b0}}), .out(operand_1_s), .sel(execute_control_bus[8]));
  Multiplexer #(.width(4), .enable("false")) multiplexer_3 (
    .in0(imm5[3:0]), .in1(reg_data_m_s), .out(sel_shift_data_s), .sel(execute_control_bus[9]));
  zcnv_unit zcnv_unit_1 (
    .data_i(data_out_o), .carry_i(carry_s), .overflow_i(overflow_s), .z_o(zcnv_unit_1_z_o[0]),
    .c_o(zcnv_unit_1_z_o[1]), .n_o(zcnv_unit_1_z_o[2]), .v_o(zcnv_unit_1_z_o[3]));
  shift shift_1 (
    .operand_i(operand_1_s), .sel_shift_data_i(sel_shift_data_s), .sel_op_shift_i(execute_control_bus[2:0]),
    .shift_data_out_o(shift_1_shift_data_out_o));
  mult_2 mult_2_1 (
    .imm5_i(imm5), .offset_incond_i(offset_incond), .offset_cond_i(offset_cond),
    .sel_mult_2_i(execute_control_bus[13:11]), .mult_2_out(mult_2_out_s));
  Register #(.width(4)) CPSR (.D(zcnv_unit_1_z_o), .en(execute_control_bus[10]), .clk(clk_i), .Q(cpsr_o), .clr(rst_i));
  alu alu_1 (
    .operand_1_i(shift_1_shift_data_out_o), .operand_2_i(operand_2_s),
    .sel_op_alu_i(execute_control_bus[5:3]), .alu_data_out_o(data_out_o), .carry_o(carry_s),
    .overflow_o(overflow_s));

  // Other names for the same wires on the sheet: imm3_s[2:0] = imm3; clk_s = clk_i; cpsr_s[3:0] = cpsr_o;
  //   data_out_s[15:0] = data_out_o; execute_control_bus_s[14:0] = execute_control_bus;
  //   sel_op_shift_s[2:0] = execute_control_bus[2:0]; sel_op_alu_s[2:0] = execute_control_bus[5:3];
  //   sel_operand_2_s[1:0] = execute_control_bus[7:6]; sel_operand_1_s = execute_control_bus[8];
  //   sel_shift_s = execute_control_bus[9]; sel_cpsr_s = execute_control_bus[10];
  //   sel_mult_s[2:0] = execute_control_bus[13:11]; execute_en_s = execute_en_i; imm5_s[4:0] = imm5;
  //   imm8_s[7:0] = imm8; offset_cond_s[7:0] = offset_cond; offset_incond_s[10:0] = offset_incond;
  //   reg_data_n_s[15:0] = reg_data_n_i; reg_data_s_s[15:0] = reg_data_s_i; rst_s = rst_i

  // Notes on the sheet:
  //   Attention, votre version de Logisim
  //   ne contient pas de tracker. Si vous
  //   enregistrez votre projet, toutes les
  //   informations du tracker seront
  //   définitivement effacées.
  //   Entité EXECUTE
  //   Sel Operand 2
  //   Sel Operand 1
  //   Sel Shift
endmodule

module mult_2 (
  input  [4:0] imm5_i,
  input  [10:0] offset_incond_i,
  input  [7:0] offset_cond_i,
  input  [2:0] sel_mult_2_i,
  output [15:0] mult_2_out
);

  wire [0:0] offset_cond_ext_signed_incr_x2_s;
  wire [15:0] imm5_ext_unsigned_s, imm5_ext_x2_s, offset_cond_ext_signed_incr_s, offset_cond_ext_signed_s,
       offset_incond_ext_signed_incr_s, offset_incond_ext_signed_incr_x2_s, offset_incond_ext_signed_s,
       offset_incond_ext_signed_shifted_incr_s, offset_incond_ext_signed_shifted_s,
       offset_incond_ext_unsigned_incr_s, offset_incond_ext_unsigned_incr_x2_s, offset_incond_ext_unsigned_s;
  wire [15:1] offset_cond_ext_signed_incr_aligned_s;

  assign imm5_ext_unsigned_s = {{11{1'b0}}, imm5_i};  // Bit_Extender bit_extender_1
  assign offset_incond_ext_signed_s = {{5{offset_incond_i[10]}}, offset_incond_i};  // Bit_Extender bit_extender_2
  assign offset_incond_ext_unsigned_s = {{5{1'b0}}, offset_incond_i};  // Bit_Extender bit_extender_3
  assign offset_cond_ext_signed_s = {{8{offset_cond_i[7]}}, offset_cond_i};  // Bit_Extender bit_extender_4
  Adder #(.width(16)) adder_1 (
    .a(offset_incond_ext_signed_s), .b(16'h2), .out(offset_incond_ext_signed_incr_s), .cin(1'b0));  // open: cout
  Adder #(.width(16)) adder_2 (
    .a(offset_cond_ext_signed_s), .b(16'h2), .out(offset_cond_ext_signed_incr_s), .cin(1'b0));  // open: cout
  Adder #(.width(16)) adder_3 (
    .a(offset_incond_ext_signed_shifted_s), .b(16'h2), .out(offset_incond_ext_signed_shifted_incr_s),
    .cin(1'b0));  // open: cout
  Adder #(.width(16)) adder_4 (
    .a(offset_incond_ext_unsigned_s), .b(16'h2), .out(offset_incond_ext_unsigned_incr_s), .cin(1'b0));  // open: cout
  Shifter #(.width(16)) shifter_1 (.in(imm5_ext_unsigned_s), .\dist (4'b0001), .out(imm5_ext_x2_s));
  Shifter #(.width(16)) shifter_2 (
    .in(offset_incond_ext_signed_incr_s), .\dist (4'b0001), .out(offset_incond_ext_signed_incr_x2_s));
  Shifter #(.width(16)) shifter_3 (
    .in(offset_cond_ext_signed_incr_s), .\dist (4'b0001),
    .out({offset_cond_ext_signed_incr_aligned_s, offset_cond_ext_signed_incr_x2_s[0]}));
  Shifter #(.width(16)) shifter_4 (
    .in(offset_incond_ext_unsigned_incr_s), .\dist (4'b0001), .out(offset_incond_ext_unsigned_incr_x2_s));
  Shifter #(.width(16)) shifter_5 (
    .in(offset_incond_ext_signed_s), .\dist (4'b1100), .out(offset_incond_ext_signed_shifted_s));
  Multiplexer #(.select(3), .width(16), .enable("false")) multiplexer_1 (
    .in0(imm5_ext_x2_s), .in1(offset_incond_ext_signed_incr_x2_s),
    .in2({offset_cond_ext_signed_incr_aligned_s, 1'b0}), .in3(offset_incond_ext_unsigned_incr_x2_s),
    .in4(imm5_ext_unsigned_s), .in5(offset_incond_ext_signed_shifted_s), .in6(offset_incond_ext_unsigned_s),
    .in7({16{1'b0}}), .out(mult_2_out), .sel(sel_mult_2_i));

  // Other names for the same wires on the sheet: imm5_s[4:0] = imm5_i; mult_2_out_s[15:0] = mult_2_out;
  //   offset_cond_ext_signed_incr_x2_s[15:1] = offset_cond_ext_signed_incr_aligned_s;
  //   offset_cond_s[7:0] = offset_cond_i; offset_incond_s[10:0] = offset_incond_i; sel_mult_2_s[2:0] = sel_mult_2_i

  // Notes on the sheet:
  //   Attention, votre version de Logisim
  //   ne contient pas de tracker. Si vous
  //   enregistrez votre projet, toutes les
  //   informations du tracker seront
  //   définitivement effacées.
  //   Extensions nécessaires
  //   Incréments
  //   x2 => shift à gauche = pas de logique
  //   Utilisé pour le BL MSB
  //   Utilisé pour le BL LSB (or logique)
endmodule

module shift (
  input  [15:0] operand_i,
  input  [3:0] sel_shift_data_i,
  input  [2:0] sel_op_shift_i,
  output [15:0] shift_data_out_o
);

  wire [15:0] asr_result_s, lsl_result_s, lsr_result_s, rsr_result_s;

  Shifter #(.width(16), .shift("ar")) shifter_1 (.in(operand_i), .\dist (sel_shift_data_i), .out(asr_result_s));
  Shifter #(.width(16)) shifter_2 (.in(operand_i), .\dist (sel_shift_data_i), .out(lsl_result_s));
  Shifter #(.width(16), .shift("lr")) shifter_3 (.in(operand_i), .\dist (sel_shift_data_i), .out(lsr_result_s));
  Shifter #(.width(16), .shift("rr")) shifter_4 (.in(operand_i), .\dist (sel_shift_data_i), .out(rsr_result_s));
  Multiplexer #(.select(3), .width(16), .enable("false")) multiplexer_1 (
    .in0(operand_i), .in1(asr_result_s), .in2(lsl_result_s), .in3(lsr_result_s), .in4(rsr_result_s),
    .in5({16{1'b0}}), .in6({16{1'b0}}), .in7({16{1'b0}}), .out(shift_data_out_o), .sel(sel_op_shift_i));

  // Other names for the same wires on the sheet: operand_s[15:0] = operand_i; sel_op_shift_s[2:0] = sel_op_shift_i;
  //   sel_shift_data_s[3:0] = sel_shift_data_i

  // Notes on the sheet:
  //   Attention, votre version de Logisim
  //   ne contient pas de tracker. Si vous
  //   enregistrez votre projet, toutes les
  //   informations du tracker seront
  //   définitivement effacées.
endmodule

module alu (
  input  [15:0] operand_1_i,
  input  [15:0] operand_2_i,
  input  [2:0] sel_op_alu_i,
  output [15:0] alu_data_out_o,
  output carry_o,
  output overflow_o
);

  wire adder_1_cout, carry_add_s, carry_sub_s, overflow_add_s, overflow_sub_s, subtractor_1_bout,
       subtractor_2_bout;
  wire [15:0] add_result_s, and_result_s, neg_result_s, not_result_s, or_result_s, sub_result_s, xor_result_s;

  Subtractor #(.width(15)) subtractor_1 (
    .a(operand_1_i[14:0]), .b(operand_2_i[14:0]), .out(sub_result_s[14:0]), .bin(1'b0),
    .bout(subtractor_1_bout));
  Subtractor #(.width(1)) subtractor_2 (
    .a(operand_1_i[15]), .b(operand_2_i[15]), .out(sub_result_s[15]), .bin(subtractor_1_bout),
    .bout(subtractor_2_bout));
  assign and_result_s = operand_1_i & operand_2_i;  // AND_Gate and_1, 16 bits wide
  assign or_result_s = operand_1_i | operand_2_i;  // OR_Gate or_1, 16 bits wide
  assign xor_result_s = operand_1_i ^ operand_2_i;  // XOR_Gate xor_1, 16 bits wide
  assign not_result_s = ~operand_1_i;  // NOT_Gate not_1, 16 bits wide
  Negator #(.width(16)) negator_1 (.in(operand_1_i), .out(neg_result_s));
  Adder #(.width(15)) adder_1 (
    .a(operand_1_i[14:0]), .b(operand_2_i[14:0]), .out(add_result_s[14:0]), .cin(1'b0), .cout(adder_1_cout));
  Adder #(.width(1)) adder_2 (
    .a(operand_1_i[15]), .b(operand_2_i[15]), .out(add_result_s[15]), .cin(adder_1_cout), .cout(carry_add_s));
  xor xor_2 (overflow_add_s, adder_1_cout, carry_add_s);
  xor xor_3 (overflow_sub_s, subtractor_1_bout, subtractor_2_bout);
  not not_2 (carry_sub_s, subtractor_2_bout);
  Multiplexer #(.select(3), .width(16), .enable("false")) multiplexer_1 (
    .in0(operand_1_i), .in1(add_result_s), .in2(sub_result_s), .in3(and_result_s), .in4(or_result_s),
    .in5(not_result_s), .in6(neg_result_s), .in7(xor_result_s), .out(alu_data_out_o), .sel(sel_op_alu_i));
  Multiplexer #(.select(2), .enable("false")) multiplexer_2 (
    .in0(1'b0), .in1(overflow_add_s), .in2(overflow_sub_s), .in3(1'b0), .out(overflow_o),
    .sel(sel_op_alu_i[1:0]));
  Multiplexer #(.select(2), .enable("false")) multiplexer_3 (
    .in0(1'b0), .in1(carry_add_s), .in2(carry_sub_s), .in3(1'b0), .out(carry_o), .sel(sel_op_alu_i[1:0]));

  // Other names for the same wires on the sheet: carry_s = carry_o; data_out_s[15:0] = alu_data_out_o;
  //   operand_1_s[15:0] = operand_1_i; operand_2_s[15:0] = operand_2_i; overflow_s = overflow_o;
  //   sel_op_alu_s[2:0] = sel_op_alu_i

  // Notes on the sheet:
  //   Attention, votre version de Logisim
  //   ne contient pas de tracker. Si vous
  //   enregistrez votre projet, toutes les
  //   informations du tracker seront
  //   définitivement effacées.
  //   ALU
  //   Sel OP ALU
endmodule

module zcnv_unit (
  input  [15:0] data_i,
  input  carry_i,
  input  overflow_i,
  output z_o,
  output c_o,
  output n_o,
  output v_o
);

  Comparator #(.width(16)) comparator_1 (.a(data_i), .b({16{1'b0}}), .eq(z_o), .lt(n_o));  // open: gt

  assign c_o = carry_i;
  assign v_o = overflow_i;

  // Other names for the same wires on the sheet: carry_s = carry_i; data_s[15:0] = data_i; overflow_s = overflow_i

  // Notes on the sheet:
  //   Attention, votre version de Logisim
  //   ne contient pas de tracker. Si vous
  //   enregistrez votre projet, toutes les
  //   informations du tracker seront
  //   définitivement effacées.
endmodule

module memory_access (
  input  [15:0] mem_data_i,
  input  [15:0] reg_data_i,
  input  [15:0] data_i,
  input  [4:0] memory_control_bus_i,
  input  rst_i,
  input  clk_i,
  input  memory_access_en_i,
  output [14:0] mem_data_adr_o,
  output [15:0] mem_adr_byte_o,
  output [15:0] mem_data_out_o,
  output [15:0] mem_out_o,
  output str_data_o,
  output ldr_data_o,
  output high_byte_o,
  output low_byte_o
);

  wire and_1_out, and_2_out, not_1_out, not_2_out, or_1_out;
  wire [15:0] register_1_q;

  or or_1 (or_1_out, memory_control_bus_i[1], memory_control_bus_i[2]);
  Multiplexer #(.width(16), .enable("false")) multiplexer_1 (
    .in0(register_1_q), .in1(data_i), .out(mem_adr_byte_o), .sel(or_1_out));
  Register #(.width(16)) register_1 (.D(mem_adr_byte_o), .en(1'b1), .clk(clk_i), .Q(register_1_q), .clr(rst_i));
  not not_1 (not_1_out, mem_adr_byte_o[0]);
  not not_2 (not_2_out, memory_control_bus_i[3]);
  and and_1 (and_1_out, memory_control_bus_i[3], mem_adr_byte_o[0]);
  and and_2 (and_2_out, memory_control_bus_i[3], not_1_out);
  Multiplexer #(.width(16), .enable("false")) multiplexer_2 (
    .in0(data_i), .in1(mem_data_i), .out(mem_out_o), .sel(memory_control_bus_i[0]));
  or or_2 (high_byte_o, not_2_out, and_1_out);
  or or_3 (low_byte_o, not_2_out, and_2_out);

  assign ldr_data_o = memory_control_bus_i[2];
  assign mem_data_adr_o = mem_adr_byte_o[15:1];
  assign mem_data_out_o = reg_data_i;
  assign str_data_o = memory_control_bus_i[1];

  // Other names for the same wires on the sheet: data_s[15:0] = data_i; high_byte_s = high_byte_o;
  //   low_byte_s = low_byte_o; adresse_offset_s = mem_adr_byte_o[0]; mem_adr_byte_s[15:0] = mem_adr_byte_o;
  //   mem_data_adr_s[14:0] = mem_adr_byte_o[15:1]; mem_data_s[15:0] = mem_data_i; mem_out_s[15:0] = mem_out_o;
  //   memory_access_en_s = memory_access_en_i; memory_control_bus_s[4:0] = memory_control_bus_i;
  //   sel_mem_s = memory_control_bus_i[0]; str_data_s = memory_control_bus_i[1]; ldr_data_s = memory_control_bus_i[2];
  //   byte_s = memory_control_bus_i[3]; mem_data_out_s[15:0] = reg_data_i; reg_data_s[15:0] = reg_data_i

  // Notes on the sheet:
  //   Attention, votre version de Logisim
  //   ne contient pas de tracker. Si vous
  //   enregistrez votre projet, toutes les
  //   informations du tracker seront
  //   définitivement effacées.
  //   Entité MEMORY ACCESS
endmodule
